# Fritzing sketch TwinTab (saved by Fritzing 0.8.3b)
stripboards: 1

parts:
  J1 = male pin header, 5 pins [form="♂ (male)"]

nets:
  GND: J1.pin1
  VCC: J1.pin2
  Extra: J1.pin3
  In: J1.pin4
  Out: J1.pin5

notes:
  http://thegaragelab.com
  -
  +
  *
  I
  O
