# Fritzing sketch 03_Power_3V3 (saved by Fritzing 0.8.3b)
stripboards: 1

parts:
  J1 = male pin header, 5 pins [form="♂ (male)"]
  PWR1 = female pin header, 2 pins [form="♀ (female)"]
  PWR2 = male pin header, 2 pins [form="♂ (male)"]
  U1 = MCP1702 Voltage Regulator [part_number="MCP1700 3V3" package="TO92 [THT]"]
  R1 = Resistor [tolerance=±5% resistance=10k package=THT]
  R2 = Resistor [tolerance=±5% resistance=10k package=THT]
  C1 = Ceramic Capacitor [capacitance=1µF package="100 mil [THT, multilayer]"]
  C2 = Ceramic Capacitor [capacitance=1µF package="100 mil [THT, multilayer]"]
  LED1 = LED - 5mm [color="Red (633nm)" package="5 mm [THT]"]
  R3 = Resistor [tolerance=±5% resistance=220 package=THT]

nets:
  GND: J1.pin1, PWR1.pin2, PWR2.pin2, U1.GND, R2.Pin_1, C1.0, C2.0
  VCC: J1.pin2, U1.Vout, C2.1, LED1.cathode, R3.Pin_1
  Extra: J1.pin3
  In: J1.pin4
  Out: J1.pin5, R1.Pin_1, R2.Pin_0
  N1: PWR1.pin1, PWR2.pin1, U1.Vin, R1.Pin_0, C1.1
  N2: LED1.anode, R3.Pin_0

notes:
  -
  +
  *
  I
  O
  Clixx Tabs, 3V3 Voltage Regulator with Battery Monitor, 1A

custom parts:
  MCP1702 Voltage Regulator: A MCP1702 Low Dropout Fixed Voltage Regulator (available in 1.2V, 1.5V, 1.8V, 2.5V, 2.8V, 3.0V, 3.3V, 4.0V, 5.0V)
